# Fritzing sketch 555_bistable+astable (saved by Fritzing 1.0.3b)
breadboards: 1

parts:
  V1 = DC Power [voltage=5V internal_resistance=0.1Ω]
  U2 = GAS_SENSOR [package=mq-3]
  R4 = Resistor [tolerance=±5% resistance=470 package="1206 [SMD]"]
  LED2 = smd LED [color="Red (633nm)" package="0603 [SMD]"]
  R5 = Resistor [tolerance=±5% resistance=10k package="1206 [SMD]"]
  R6 = Resistor [tolerance=±5% resistance=10k package="1206 [SMD]"]
  S1 = SWITCH-MOMENTARY-2 [package=tactile_switch_smd-2]
  C1 = Ceramic Capacitor [capacitance=0.01µF voltage=10V package="100 mil [THT, multilayer]"]
  U1 = 555 Timer [package="SO8 [SMD]"]
  U3 = 555 Timer [package="SO8 [SMD]"]
  C2 = Ceramic Capacitor [capacitance=0.01µF voltage=10V package="100 mil [THT, multilayer]"]
  R7 = Resistor [tolerance=±5% resistance=10k package="1206 [SMD]"]
  R8 = Resistor [tolerance=±5% resistance=10k package="1206 [SMD]"]
  C3 = Ceramic Capacitor [capacitance=0.01µF voltage=10V package="100 mil [THT, multilayer]"]
  C4 = Capacitor Polarized [package=cpol-radial-10uf-25v]
  J1 = Piezo Speaker [mn=Piezo]

nets:
  N1: V1.V-, U2.A1, R4.Pin_0, S1.2, C1.0, U1.Pin_1, U1.Pin_6, U3.Pin_1, C2.0, C3.0, J1.pin2
  N2: V1.V+, U2.B1, R5.Pin_0, R6.Pin_0, U1.Pin_8, U3.Pin_4, U3.Pin_8, R7.Pin_0
  N3: U2.H1, R5.Pin_1, U1.Pin_2
  N4: R4.Pin_1, LED2.cathode
  N5: LED2.anode, U1.Pin_3
  N6: R6.Pin_1, S1.1, U1.Pin_4
  N7: C1.1, U1.Pin_5
  N8: U3.Pin_2, U3.Pin_6, C2.1, R8.Pin_1
  N9: U3.Pin_3, C4.-
  N10: U3.Pin_5, C3.1
  N11: U3.Pin_7, R7.Pin_1, R8.Pin_0
  N12: C4.+, J1.pin1
