# Fritzing sketch 555_ir_sensor_solenoid_voltage_regulator (saved by Fritzing 1.0.2b)
breadboards: 1

parts:
  IR_sensor = ky-033 [package=THT]
  L1 = Solenoid [mpn="Solenoid Lock" part_number="12v 0.8A"]
  U1 = 555 Timer [part_number=TLC555 package="DIP8 [THT]"]
  Power_12v = Power plug
  U1_2 = Voltage Regulator - 5V [package="TO220 [THT]"]
  Q1 = Basic FET N-Channel [mpn=IRLB3034 package="D2Pak [SMD]"]
  S1 = SWITCH-MOMENTARY-2 [package=tactile-pth-12mm]
  R1 = Resistor [tolerance=±5% power=0.25W resistance=10k package=THT]
  C1 = Ceramic Capacitor [capacitance=10nF voltage=35V package="1206 [SMD, multilayer]"]
  R2 = Resistor [tolerance=±5% power=0.25W resistance=10k package=THT]
  R3 = 6mm Trimmer Potentiometer [maximum_resistance=500kΩ knob_status=50% power=0.5W package=THT]
  C2 = Ceramic Capacitor [capacitance=10µF voltage=35V package="1206 [SMD, multilayer]"]
  D1 = Schottky Diode [part_number=1N5822 package="300 mil [THT]"]

nets:
  N1: IR_sensor.pin2, U1.Trigger
  GND: IR_sensor.pin3, Power_12v.GND, U1_2.GND
  N2: IR_sensor.pin4, U1.Vcc_Supply_Voltage, U1_2.output_voltage, R1.Pin_0, R3.leg1
  N3: L1.pin1, Power_12v.VCC, U1_2.input_voltage, D1.cathode
  N4: L1.pin2, Q1.drain, D1.anode
  GND_2: U1.Ground, Q1.source, S1.2, C1.0, C2.0
  N5: U1.Output, Q1.Gate
  N6: U1.Reset, S1.1, R1.Pin_1
  N7: U1.Control_Voltage, C1.1
  N8: U1.Threshold, U1.Discharge, R2.Pin_1, C2.1
  N9: R2.Pin_0, R3.wiper

custom parts:
  ky-033: KY-033 Line successor module with TCRT5000 and analog output.
