# Fritzing sketch 555_monostable_diode (saved by Fritzing 1.0.2b)
breadboards: 1

parts:
  U1 = 555 Timer [part_number=TLC555 package="DIP8 [THT]"]
  S2 = SWITCH-MOMENTARY-2 [package=tactile-pth-12mm]
  R4 = Resistor [tolerance=±5% power=0.25W resistance=10k package=THT]
  C1 = Ceramic Capacitor [capacitance=0.01µF voltage=35V package="1206 [SMD, multilayer]"]
  R2 = Resistor [tolerance=±5% power=0.25W resistance=10k package=THT]
  R3 = 6mm Trimmer Potentiometer [maximum_resistance=500kΩ knob_status=50% power=0.5W package=THT]
  C2 = Ceramic Capacitor [capacitance=10µF voltage=35V package="1206 [SMD, multilayer]"]
  R1 = Resistor [tolerance=±5% power=0.25W resistance=10k package=THT]
  S1 = SWITCH-MOMENTARY-2 [package=tactile-pth-12mm]
  LED1 = LED - 5mm [color="Red (633nm)" current=0.030A package="5 mm [THT]"]
  R5 = Resistor [tolerance=±5% power=0.25W resistance=470 package=THT]

nets:
  GND: U1.Ground, S2.2, C1.0, C2.0, S1.1, R5.Pin_1
  N1: U1.Trigger, R1.Pin_1, S1.2
  N2: U1.Output, LED1.anode
  N3: U1.Reset, S2.1, R4.Pin_1
  N4: U1.Control_Voltage, C1.1
  N5: U1.Threshold, U1.Discharge, R2.Pin_1, C2.1
  N6: U1.Vcc_Supply_Voltage, R4.Pin_0, R3.leg1
  N7: R2.Pin_0, R3.wiper
  9V: R1.Pin_0
  N8: LED1.cathode, R5.Pin_0
